# Fritzing sketch IRPeripheral (saved by Fritzing 0.9.2b)
breadboards: 1

parts:
  Part2 = Arduino Nano (Rev3.0) (ICSP)
  D1 = LTE-302 [package=lte-302]
  Q1 = NPN-Transistor [package="TO92 [THT]"]
  R1 = Resistor [tolerance=±5% resistance=220 package="2512 [SMD]"]

nets:
  N1: Part2.GND, Q1.E
  N2: Part2.D3, R1.Pin_0
  N3: Part2.5V, D1.A
  N4: D1.C, Q1.B
  N5: Q1.C, R1.Pin_1
